# Fritzing sketch raspberry-pi-soda (saved by Fritzing 0.9.5d)
stripboards: 2

parts:
  Raspberry_Pi_1 = Raspberry Pi 3 [part_number=RPI-3-V1.2]
  LED1 = LED - 5mm [color="Blue (430nm)" package="5 mm [THT]"]
  LED2 = LED - 5mm [color="Yellow (585nm)" package="5 mm [THT]"]
  LED3 = LED - 5mm [color="Red (633nm)" package="5 mm [THT]"]
  LED4 = LED - 5mm [color="Green (555nm)" package="5 mm [THT]"]
  S2 = Round Pushbutton
  S3 = Round Pushbutton
  S4 = Round Pushbutton
  S5 = Round Pushbutton

nets:
  N1: Raspberry_Pi_1.GPIO17, S2.leg0
  N2: Raspberry_Pi_1.GPIO27, S3.leg0
  N3: Raspberry_Pi_1.GPIO22, S4.leg0
  N4: Raspberry_Pi_1.GPIO6, LED4.cathode
  N5: Raspberry_Pi_1.GPIO13, LED3.cathode
  N6: Raspberry_Pi_1.GPIO19, LED2.cathode
  N7: Raspberry_Pi_1.GPIO26, LED1.cathode
  N8: Raspberry_Pi_1.GND, LED1.anode, LED2.anode, LED3.anode, LED4.anode, S2.leg1, S3.leg1, S4.leg1, S5.leg1
  N9: Raspberry_Pi_1.GPIO23, S5.leg0

notes:
  Button 4
  Button 3
  Button 2
  Button 1
  LED 1
  LED 2
  LED 3
  LED 4
